// Digital circuit atk16.dig as structural Verilog
module atk16 (
  input  IN,
  input  clk,
  output OUT
);

  wire ALU_OE, FR_IE, IM_M, IR_IE, IRQ0_out, LI_OE, MAR_IE, MEM_IE, MEM_OE, not_1_out, or_1_out, PC_CO,
       PC_IE, PC_OE, R1_OE, R2_OE, reset_1_out, RW_IE, US_RS;
  wire [2:0] atk16_decoder_1_alu_s, atk16_decoder_1_r1_s, atk16_decoder_1_r2_s, FLAG_EQ, Microsequencer_out;
  wire [3:0] ALU_flags, FR_Q, OPCODE;
  wire [3:3] bitselector_1_out;
  wire [14:14] UCODE_d;
  wire [15:0] ALU_y, atk16_alu_inputs_1_a, atk16_alu_inputs_1_b, atk16_jump_unit_1_pc_res,
       atk16_regbank_1_d1, atk16_regbank_1_d2, driver_1_out, MAR_q, PC_out;

  atk16_decoder atk16_decoder_1 (
    .DBUS(driver_1_out), .IR_IE(IR_IE), .CLK(clk), .LI_OE(LI_OE), .OP(OPCODE), .RW_S(FLAG_EQ),
    .ALU_S(atk16_decoder_1_alu_s), .R1_S(atk16_decoder_1_r1_s), .R2_S(atk16_decoder_1_r2_s));
  Reset #(.invertOutput("false")) reset_1 (.out(reset_1_out));
  atk16_jump_unit atk16_jump_unit_1 (.ADDR(driver_1_out), .PC(PC_out), .IM_M(IM_M), .PC_RES(atk16_jump_unit_1_pc_res));
  not not_1 (not_1_out, clk);
  or or_1 (or_1_out, US_RS, reset_1_out);
  DipSwitch IRQ0 (.out(IRQ0_out));
  Counter #(.Bits(3)) Microsequencer (.en(1'b1), .C(not_1_out), .clr(or_1_out), .out(Microsequencer_out));  // open: ovf
  CounterPreset #(.Bits(16), .isProgramCounter("true")) PC (
    .en(PC_CO), .C(clk), .dir(1'b0), .in(atk16_jump_unit_1_pc_res), .ld(PC_IE), .clr(1'b0), .out(PC_out));  // open: ovf
  atk16_regbank atk16_regbank_1 (
    .Din(driver_1_out), .RW_IE(RW_IE), .RW_S(FLAG_EQ), .CLK(clk), .R1_S(atk16_decoder_1_r1_s),
    .R2_S(atk16_decoder_1_r2_s), .D1(atk16_regbank_1_d1), .D2(atk16_regbank_1_d2));
  BitSelector #(.Selector_Bits(2)) bitselector_1 (.in(FR_Q), .sel(FLAG_EQ[1:0]), .out(bitselector_1_out[3]));
  assign driver_1_out = PC_OE ? PC_out : 16'bz;  // Driver driver_1
  EEPROM #(.AddrBits(8), .Bits(16)) UCODE (
    .A({OPCODE, bitselector_1_out[3], Microsequencer_out}), .CS(1'b1), .WE(1'b0), .OE(1'b1),
    .D({US_RS, UCODE_d[14], FR_IE, ALU_OE, LI_OE, IM_M, IR_IE, R2_OE, R1_OE, RW_IE, MEM_OE, MEM_IE, MAR_IE, PC_OE, PC_IE, PC_CO}));
  // Probe OPCODE on OPCODE
  // Probe PC on PC_out
  // Probe Bus on driver_1_out
  assign driver_1_out = R1_OE ? atk16_regbank_1_d1 : 16'bz;  // Driver driver_2
  assign driver_1_out = R2_OE ? atk16_regbank_1_d2 : 16'bz;  // Driver driver_3
  atk16_alu_inputs atk16_alu_inputs_1 (
    .R1(atk16_regbank_1_d1), .R2(atk16_regbank_1_d2), .R2_S(atk16_decoder_1_r2_s), .IM_M(IM_M),
    .A(atk16_alu_inputs_1_a), .B(atk16_alu_inputs_1_b));
  Register #(.Bits(16)) MAR (.D(driver_1_out), .C(clk), .en(MAR_IE), .Q(MAR_q));
  atk16_alu ALU (
    .A(atk16_alu_inputs_1_a), .B(atk16_alu_inputs_1_b), .S(atk16_decoder_1_alu_s), .Y(ALU_y),
    .FLAGS(ALU_flags));
  Stop stop_1 (.stop(UCODE_d[14]));
  atk16_mem atk16_mem_1 (.ADDR(MAR_q), .DBUS(driver_1_out), .MEM_IE(MEM_IE), .MEM_OE(MEM_OE));
  Break break_1 (.brk(clk));
  assign driver_1_out = ALU_OE ? ALU_y : 16'bz;  // Driver driver_4
  Register #(.Bits(4)) FR (.D(ALU_flags), .C(clk), .en(FR_IE), .Q(FR_Q));

  assign OUT = 1'b0;
  // also tied to GND on the sheet: IN

  // Notes on the sheet:
  //   OUT: Dummy output
  //   clk: Hz: 50
  //   contents of UCODE (hex, n*v repeats v):
  //   c,221,3040,8000,4*0,c,221,3040,8000,4*0,c,221,3440,8000,4*0,c
  //   ,221,3440,8000,4*0,c,221,88,60,8000,0,0,0,c,221,88,60,8000,0,0,0
  //   ,c,221,88,110,8000,0,0,0,c,221,88,110,8000,0,0,0,c,221,840,8000
  //   ,4*0,c,221,840,8000,4*0,c,221,82,8000,4*0,c,221,82,8000,4*0,c
  //   ,221,c02,8000,4*0,c,221,c02,8000,4*0,c,221,8000,5*0,c,221,82,8000
  //   ,4*0,c,221,8000,5*0,c,221,c02,8000,4*0,c,221,44,8000,4*0,c,221
  //   ,44,8000,4*0,c,221,8000,5*0,c,221,8000,5*0,c,221,8000,5*0,c,221
  //   ,8000,5*0,c,221,8000,5*0,c,221,8000,5*0,c,221,8000,5*0,c,221,8000
  //   ,5*0,c,221,8000,5*0,c,221,8000,5*0,c,221,4000,5*0,c,221,4000
endmodule

/* Test case Sum program TODO:
IN OUT

program(0x4051, 0x40a2, 0x029b)

0 x
*/
