// Digital circuit atk16_tpu.dig as structural Verilog
module atk16_tpu (
  input  [12:0] MMIO_S,
  input  MMIO_IE,
  input  MMIO_OE,
  input  PCLK,
  input  CLK,
  input  [15:0] DBUS,
  input  [8:0] X,
  input  [7:0] Y,
  output [1:0] PR,
  output [1:0] PG,
  output [1:0] PB
);

  wire [7:0] CHAR_S, CHARMEM_d;

  RAMDualPort #(.AddrBits(11), .Bits(8)) TEXTMEM (
    .A({X[5:0], Y[4:0]}), .Din({8{1'b0}}), .str(1'b0), .C(CLK), .ld(1'b1), .D(CHAR_S));
  ROM #(.AddrBits(11), .Bits(8)) CHARMEM (.A({Y[7:5], CHAR_S}), .sel(1'b1), .D(CHARMEM_d));
  BitSelector #(.Selector_Bits(3)) bitselector_1 (.in(CHARMEM_d), .sel(X[8:6]), .out(PB[1]));

  assign PB[0] = PB[1];
  assign PG = {2{PB[1]}};
  assign PR = {2{PB[1]}};

  // Other names for the same wires on the sheet: CCOLOR = PB[1]; TX[5:0] = X[5:0]; CX[2:0] = X[8:6]; TY[4:0] = Y[4:0];
  //   CY[2:0] = Y[7:5]

  // Notes on the sheet:
  //   MMIO_S: MMI/O selector
  //   PCLK: Pixel clock
  //   CLK: CPU clock
  //   DBUS: Data bus
  //   X: X pixel
  //   Y: Y pixel
endmodule
